// Logisim project CD_TF.circ as structural Verilog: 3 circuits, main circuit main
module main (
);

  Alvo alvo_1 ();  // open: A, B, C, D, S1, S2, S3, S4
endmodule

module Alvo (
  input  A,
  input  B,
  input  C,
  input  D,
  output S1,
  output S2,
  output S3,
  output S4
);

  wire and_1_out, and_2_out, and_3_out, and_4_out, and_5_out, and_6_out, and_7_out, and_8_out, and_9_out,
       and_10_out, and_11_out, and_12_out, and_13_out, and_14_out, and_15_out, and_16_out, not_1_out,
       not_2_out, not_3_out, not_4_out;

  not not_1 (not_1_out, A);
  not not_2 (not_2_out, B);
  not not_3 (not_3_out, C);
  not not_4 (not_4_out, D);
  and and_1 (and_1_out, not_2_out, not_3_out, not_4_out);
  and and_2 (and_2_out, not_1_out, not_2_out, C);
  and and_3 (and_3_out, B, not_3_out, D);
  and and_4 (and_4_out, A, B, C);
  and and_5 (and_5_out, not_1_out, C);
  and and_6 (and_6_out, not_1_out, B, not_4_out);
  and and_7 (and_7_out, B, C);
  and and_8 (and_8_out, A, not_2_out, not_3_out, D);
  and and_9 (and_9_out, not_2_out, not_4_out);
  and and_10 (and_10_out, not_1_out, C, not_4_out);
  and and_11 (and_11_out, not_2_out, C);
  and and_12 (and_12_out, A, not_2_out);
  and and_13 (and_13_out, not_1_out, not_2_out, not_3_out);
  and and_14 (and_14_out, not_1_out, not_4_out);
  and and_15 (and_15_out, A, C, D);
  and and_16 (and_16_out, A, B, D);
  or or_1 (S1, and_1_out, and_2_out, and_3_out, and_4_out);
  or or_2 (S2, and_5_out, and_6_out, and_7_out, and_8_out);
  or or_3 (S3, and_9_out, and_10_out, and_11_out, and_12_out);
  or or_4 (S4, and_13_out, and_14_out, and_15_out, and_16_out);
endmodule

module Navio (
);

  Comparator #(.width(1)) comparator_1 ();  // open: a, b, gt, eq, lt
  Comparator #(.width(1)) comparator_2 ();  // open: a, b, gt, eq, lt
  Comparator #(.width(1)) comparator_3 ();  // open: a, b, gt, eq, lt
  Comparator #(.width(1)) comparator_4 ();  // open: a, b, gt, eq, lt
endmodule
