// Digital circuit FSM.dig as structural Verilog
module FSM (
  input  in_2,
  output [2:0] out_1
);

  Counter #(.applicationType("GHDL"), .CodeFile("D:\\Downloads\\Digital\\SISTEMAS DIGITAIS\\FSM.vhd")) u_Counter (
    .S(in_2), .Y(out_1));
endmodule
