// Digital circuit Main.dig as structural Verilog
module Main (
  input  coin
);

  wire clock_out, reset_out, u_SodaMachine_dispense_out;

  Button reset (.out(reset_out));
  Button clock (.out(clock_out));
  SodaMachine #(.applicationType("GHDL"), .CodeFile("C:\\Users\\richa\\OneDrive\\Área de Trabalho\\vhdl\\Elevador.vhd")) u_SodaMachine (
    .clk(clock_out), .reset(reset_out), .coin(coin), .dispense_out(u_SodaMachine_dispense_out));
  LED led_1 (.in(u_SodaMachine_dispense_out));
endmodule
